# Fritzing sketch Arduino Driving Peltier Up Down (saved by Fritzing 0.7.12b)
breadboards: 1

parts:
  Arduino2 = Arduino
  Q1 = Basic FET P-Channel [package="TO220 [THT]"]
  J1 = Peltier Element
  VCC2 = Battery block 9V
  S1_-_Down = Pushbutton [package="[THT]"]
  S2_Up = Pushbutton [package="[THT]"]
  R1 = Resistor [tolerance=±5% resistance=220 package=THT]
  R2 = Resistor [tolerance=±5% resistance=220 package=THT]

nets:
  N1: Arduino2.D8, S2_Up.Pin_1, S2_Up.Pin_2, R2.Pin_0
  N2: Arduino2.D7, S1_-_Down.Pin_1, S1_-_Down.Pin_2, R1.Pin_0
  N3: Arduino2.D3, Q1.gate
  N4: Arduino2.GND, J1.pin1, VCC2.-, R1.Pin_1, R2.Pin_1
  N5: Arduino2.VIN, Q1.drain, VCC2.+, S1_-_Down.Pin_3, S1_-_Down.Pin_4, S2_Up.Pin_3, S2_Up.Pin_4
  N6: Q1.source, J1.pin2

notes:
  P8 is Up,
  P7 is Down,
