# Fritzing sketch Arduino Driving Peltier (saved by Fritzing 0.7.12b)
breadboards: 1

parts:
  Arduino2 = Arduino
  Q1 = Basic FET P-Channel [package="TO220 [THT]"]
  J1 = Peltier Element
  VCC2 = Battery block 9V

nets:
  N1: Arduino2.D3, Q1.gate
  N2: Arduino2.GND, J1.pin1, VCC2.-
  N3: Arduino2.VIN, Q1.drain, VCC2.+
  N4: Q1.source, J1.pin2
