# Fritzing sketch Peltier Driven from MosFET (saved by Fritzing 0.7.12b)
breadboards: 1

parts:
  Q1_-_IRF9540N = Basic FET P-Channel [part_number=IRF9540N package="TO220 [THT]"]
  J1 = Peltier Element
  R1 = Resistor [tolerance=±5% resistance=220 package=THT]
  R2 = Resistor [tolerance=±5% resistance=220 package=THT]
  VCC1 = Battery block 9V

nets:
  N1: Q1_-_IRF9540N.gate, R1.Pin_0, R2.Pin_1
  N2: Q1_-_IRF9540N.drain, R2.Pin_0, VCC1.+
  N3: Q1_-_IRF9540N.source, J1.pin2
  N4: J1.pin1, R1.Pin_1, VCC1.-

notes:
  Vgs should be 4.5V
  Pins are G, D, S
